// Logisim project ep1bool.circ as structural Verilog
module ep1 (
  input  a,
  input  b,
  input  c,
  input  d
);

  wire and_1_out, and_2_out, and_3_out, and_4_out, and_5_out, and_6_out, and_7_out, and_8_out, and_9_out,
       and_10_out, and_11_out, and_12_out, and_13_out, and_14_out, and_15_out, and_16_out, and_17_out,
       not_1_out, not_2_out, not_3_out, not_4_out, not_5_out, not_6_out, not_7_out, not_8_out, not_9_out,
       not_10_out, not_11_out, not_12_out, not_13_out, not_14_out, not_15_out, not_16_out, not_17_out,
       not_18_out, not_19_out, not_20_out, not_21_out, or_1_out, or_2_out, or_3_out, or_4_out, or_5_out,
       or_6_out, or_7_out, or_8_out, or_9_out, or_10_out, or_11_out, or_12_out, or_13_out, or_14_out,
       or_15_out, or_16_out, or_17_out, or_18_out;

  not not_1 (not_1_out, b);
  not not_2 (not_2_out, c);
  and and_1 (and_1_out, not_2_out, not_3_out);
  not not_3 (not_3_out, d);
  not not_4 (not_4_out, b);
  and and_2 (and_2_out, not_4_out, not_5_out);
  not not_5 (not_5_out, d);
  and and_3 (and_3_out, b, d);
  not not_6 (not_6_out, c);
  and and_4 (and_4_out, not_6_out, not_7_out);
  not not_7 (not_7_out, d);
  and and_5 (and_5_out, b, not_8_out);
  not not_8 (not_8_out, c);
  and and_6 (and_6_out, b, not_9_out);
  not not_9 (not_9_out, d);
  not not_10 (not_10_out, b);
  and and_7 (and_7_out, not_10_out, c);
  and and_8 (and_8_out, c, not_11_out);
  not not_11 (not_11_out, d);
  and and_9 (and_9_out, b, not_12_out);
  not not_12 (not_12_out, c);
  not not_13 (not_13_out, b);
  and and_10 (and_10_out, not_13_out, not_14_out);
  not not_14 (not_14_out, d);
  and and_11 (and_11_out, c, not_15_out);
  not not_15 (not_15_out, d);
  not not_16 (not_16_out, b);
  and and_12 (and_12_out, not_16_out, not_17_out);
  not not_17 (not_17_out, d);
  not not_18 (not_18_out, b);
  and and_13 (and_13_out, not_18_out, c);
  not not_19 (not_19_out, d);
  and and_14 (and_14_out, b, not_20_out);
  not not_20 (not_20_out, c);
  not not_21 (not_21_out, c);
  or or_1 (or_1_out, not_21_out, d);
  or or_2 (or_2_out, not_1_out, and_1_out);
  and and_15 (and_15_out, c, d);
  or or_3 (or_3_out, and_2_out, c);
  or or_4 (or_4_out, and_3_out, a);
  or or_5 (or_5_out, and_4_out, and_5_out);
  or or_6 (or_6_out, and_6_out, a);
  or or_7 (or_7_out, and_7_out, and_8_out);
  or or_8 (or_8_out, and_9_out, a);
  or or_9 (or_9_out, and_10_out, and_11_out);
  or or_10 (or_10_out, and_12_out, and_13_out);
  and and_16 (and_16_out, c, not_19_out);
  and and_17 (and_17_out, and_14_out, d);
  or or_11 (or_11_out, or_1_out, b);
  or or_12 (or_12_out, or_2_out, and_15_out);
  or or_13 (or_13_out, or_3_out, or_4_out);
  or or_14 (or_14_out, or_5_out, or_6_out);
  or or_15 (or_15_out, or_7_out, or_8_out);
  or or_16 (or_16_out, or_10_out, and_16_out);
  or or_17 (or_17_out, and_17_out, a);
  or or_18 (or_18_out, or_16_out, or_17_out);
  _7_Segment_Display u_7_segment_display_1 (
    .g(or_15_out), .f(or_14_out), .a(or_13_out), .b(or_12_out), .e(or_9_out), .d(or_18_out), .c(or_11_out));  // open: dp
endmodule
