// Logisim project tentativa1.circ as structural Verilog: 4 circuits, main circuit main
module main (
);

  Adder #(.width(4)) adder_1 ();  // open: a, b, out, cin, cout
endmodule

module ep2 (
  input  in_1,
  input  in_2,
  input  in_3,
  input  in_4,
  input  in_5,
  input  in_6,
  input  in_7,
  input  in_8,
  output out_9,
  output out_10,
  output out_11,
  output out_12,
  output out_13
);

  wire sum1_first_circuit_1_cout, sum1d_1_cout, sum1d_2_cout;

  sum1_first_circuit sum1_first_circuit_1 (.a(in_1), .b(in_5), .s(out_9), .cout(sum1_first_circuit_1_cout));
  sum1d sum1d_1 (.a(in_2), .b(in_6), .cin(sum1_first_circuit_1_cout), .s(out_10), .cout(sum1d_1_cout));
  sum1d sum1d_2 (.a(in_3), .b(in_7), .cin(sum1d_1_cout), .s(out_11), .cout(sum1d_2_cout));
  sum1d sum1d_3 (.a(in_4), .b(in_8), .cin(sum1d_2_cout), .s(out_12), .cout(out_13));
endmodule

module sum1d (
  input  a,
  input  b,
  input  cin,
  output s,
  output cout
);

  wire and_1_out, and_2_out, and_3_out, and_4_out, and_5_out, and_6_out, and_7_out, not_1_out, not_2_out,
       not_3_out, not_4_out, not_5_out, not_6_out;

  not not_1 (not_1_out, a);
  not not_2 (not_2_out, b);
  not not_3 (not_3_out, a);
  not not_4 (not_4_out, cin);
  not not_5 (not_5_out, b);
  not not_6 (not_6_out, cin);
  and and_1 (and_1_out, b, cin);
  and and_2 (and_2_out, a, cin);
  and and_3 (and_3_out, a, b);
  and and_4 (and_4_out, not_1_out, not_2_out, cin);
  and and_5 (and_5_out, not_3_out, b, not_4_out);
  and and_6 (and_6_out, a, not_5_out, not_6_out);
  and and_7 (and_7_out, a, b, cin);
  or or_1 (cout, and_1_out, and_2_out, and_3_out);
  or or_2 (s, and_4_out, and_5_out, and_6_out, and_7_out);
endmodule

module sum1_first_circuit (
  input  a,
  input  b,
  output s,
  output cout
);

  wire and_2_out, and_3_out, not_1_out, not_2_out;

  not not_1 (not_1_out, a);
  not not_2 (not_2_out, b);
  and and_1 (cout, a, b);
  and and_2 (and_2_out, not_1_out, b);
  and and_3 (and_3_out, a, not_2_out);
  or or_1 (s, and_2_out, and_3_out);
endmodule
