// Logisim project tentativa2.circ as structural Verilog
module subt1_first (
  input  a,
  input  b,
  output s,
  output cout
);

  wire and_1_out, and_2_out, not_1_out, not_2_out, not_3_out;

  not not_1 (not_1_out, a);
  not not_2 (not_2_out, b);
  not not_3 (not_3_out, a);
  and and_1 (and_1_out, not_1_out, b);
  and and_2 (and_2_out, a, not_2_out);
  and and_3 (cout, not_3_out, b);
  or or_1 (s, and_1_out, and_2_out);
endmodule

module subt (
  input  a,
  input  b,
  input  cin,
  output s,
  output cout
);

  wire and_1_out, and_2_out, and_3_out, and_4_out, and_5_out, and_6_out, and_7_out, not_1_out, not_2_out,
       not_3_out, not_4_out, not_5_out, not_6_out, not_7_out, not_8_out;

  not not_1 (not_1_out, a);
  not not_2 (not_2_out, b);
  not not_3 (not_3_out, a);
  not not_4 (not_4_out, cin);
  not not_5 (not_5_out, b);
  not not_6 (not_6_out, cin);
  not not_7 (not_7_out, a);
  not not_8 (not_8_out, a);
  and and_1 (and_1_out, not_1_out, not_2_out, cin);
  and and_2 (and_2_out, not_3_out, b, not_4_out);
  and and_3 (and_3_out, a, not_5_out, not_6_out);
  and and_4 (and_4_out, a, b, cin);
  and and_5 (and_5_out, not_7_out, cin);
  and and_6 (and_6_out, not_8_out, b);
  and and_7 (and_7_out, b, cin);
  or or_1 (s, and_1_out, and_2_out, and_3_out, and_4_out);
  or or_2 (cout, and_5_out, and_6_out, and_7_out);
endmodule

module sum1_first (
  input  a,
  input  b,
  output s,
  output cout
);

  wire and_2_out, and_3_out, not_1_out, not_2_out;

  not not_1 (not_1_out, a);
  not not_2 (not_2_out, b);
  and and_1 (cout, a, b);
  and and_2 (and_2_out, not_1_out, b);
  and and_3 (and_3_out, a, not_2_out);
  or or_1 (s, and_2_out, and_3_out);
endmodule

module sum1 (
  input  a,
  input  b,
  input  cin,
  output s,
  output cout
);

  wire and_1_out, and_2_out, and_3_out, and_4_out, and_5_out, and_6_out, and_7_out, not_1_out, not_2_out,
       not_3_out, not_4_out, not_5_out, not_6_out;

  not not_1 (not_1_out, a);
  not not_2 (not_2_out, b);
  not not_3 (not_3_out, a);
  not not_4 (not_4_out, cin);
  not not_5 (not_5_out, b);
  not not_6 (not_6_out, cin);
  and and_1 (and_1_out, b, cin);
  and and_2 (and_2_out, a, cin);
  and and_3 (and_3_out, a, b);
  and and_4 (and_4_out, not_1_out, not_2_out, cin);
  and and_5 (and_5_out, not_3_out, b, not_4_out);
  and and_6 (and_6_out, a, not_5_out, not_6_out);
  and and_7 (and_7_out, a, b, cin);
  or or_1 (cout, and_1_out, and_2_out, and_3_out);
  or or_2 (s, and_4_out, and_5_out, and_6_out, and_7_out);
endmodule

module total_sum (
  input  [3:0] in_1,
  input  [3:0] in_2,
  output [3:0] out_3,
  output out_4
);

  wire sum1_1_cout, sum1_2_cout, sum1_first_1_cout;

  sum1_first sum1_first_1 (.a(in_1[0]), .b(in_2[0]), .s(out_3[0]), .cout(sum1_first_1_cout));
  sum1 sum1_1 (.a(in_1[1]), .b(in_2[1]), .cin(sum1_first_1_cout), .s(out_3[1]), .cout(sum1_1_cout));
  sum1 sum1_2 (.a(in_1[2]), .b(in_2[2]), .cin(sum1_1_cout), .s(out_3[2]), .cout(sum1_2_cout));
  sum1_last sum1_last_1 (.a(in_1[3]), .b(in_2[3]), .cin(sum1_2_cout), .s(out_3[3]), .cout(out_4));
endmodule

module sum1_last (
  input  a,
  input  b,
  input  cin,
  output s,
  output cout
);

  wire and_1_out, and_2_out, and_3_out, and_4_out, not_1_out, not_2_out, not_3_out, not_4_out, not_5_out,
       not_6_out;

  not not_1 (not_1_out, a);
  not not_2 (not_2_out, b);
  not not_3 (not_3_out, a);
  not not_4 (not_4_out, cin);
  not not_5 (not_5_out, b);
  not not_6 (not_6_out, cin);
  or or_1 (cout, cin, b, a);
  and and_1 (and_1_out, not_1_out, not_2_out, cin);
  and and_2 (and_2_out, not_3_out, b, not_4_out);
  and and_3 (and_3_out, a, not_5_out, not_6_out);
  and and_4 (and_4_out, a, b, cin);
  or or_2 (s, and_1_out, and_2_out, and_3_out, and_4_out);
endmodule

module total_subt (
  input  [3:0] in_1,
  input  [3:0] in_2,
  output [3:0] out_3,
  output out_4
);

  wire subt1_first_1_cout, subt_1_cout, subt_2_cout;

  subt1_first subt1_first_1 (.a(in_1[0]), .b(in_2[0]), .s(out_3[0]), .cout(subt1_first_1_cout));
  subt subt_1 (.a(in_1[1]), .b(in_2[1]), .cin(subt1_first_1_cout), .s(out_3[1]), .cout(subt_1_cout));
  subt subt_2 (.a(in_1[2]), .b(in_2[2]), .cin(subt_1_cout), .s(out_3[2]), .cout(subt_2_cout));
  subt_last subt_last_1 (.a(in_1[3]), .b(in_2[3]), .cin(subt_2_cout), .s(out_3[3]), .cout(out_4));
endmodule

module subt_last (
  input  a,
  input  b,
  input  cin,
  output s,
  output cout
);

  wire and_1_out, and_2_out, and_3_out, and_4_out, not_1_out, not_2_out, not_3_out, not_4_out, not_5_out;

  not not_1 (not_1_out, b);
  not not_2 (not_2_out, a);
  not not_3 (not_3_out, cin);
  not not_4 (not_4_out, b);
  not not_5 (not_5_out, b);
  and and_1 (and_1_out, not_1_out, cin);
  and and_2 (and_2_out, not_2_out, b, not_3_out);
  and and_3 (and_3_out, a, not_4_out);
  and and_4 (and_4_out, a, cin);
  and and_5 (cout, a, not_5_out, cin);
  or or_1 (s, and_1_out, and_2_out, and_3_out, and_4_out);
endmodule
