// Logisim project logisim_master_slave.circ as structural Verilog: 1 circuit, main circuit main
module main (
  input  in_1,
  input  in_2,
  input  in_3,
  output out_4,
  output out_5
);

  wire not_1_out, s_r_ff_1_q, s_r_ff_1_qn;

  S_R_Flip_Flop s_r_ff_1 (.S(in_1), .clk(in_3), .R(in_2), .Q(s_r_ff_1_q), .Qn(s_r_ff_1_qn));  // open: preset, reset, en
  not not_1 (not_1_out, in_3);
  S_R_Flip_Flop s_r_ff_2 (
    .S(s_r_ff_1_q), .clk(not_1_out), .R(s_r_ff_1_qn), .Q(out_4), .Qn(out_5));  // open: preset, reset, en
endmodule
